// Logisim project CPU.circ as structural Verilog: 20 circuits, main circuit main
module main (
  output [3:0] out_1,
  output [3:0] out_2,
  output [1:0] out_3,
  output [1:0] out_4,
  output [2:0] out_5,
  output [2:0] out_6,
  output [2:0] out_7,
  output [3:0] out_8,
  output [3:0] out_9,
  output out_10,
  output out_11,
  output out_12,
  output [1:0] out_13,
  output [1:0] out_14
);

  wire alu_1_overflow, alu_1_zero, and_1_out, and_2_out, and_3_out, and_4_out, and_5_out, and_6_out,
       and_7_out, and_8_out, and_9_out, and_10_out, and_11_out, clock_1_out, controlunit_1_out_4,
       controlunit_1_stop, cu_steps_1_step1, cu_steps_1_step2, cu_steps_1_step3, cu_steps_1_step4,
       decod_er_1_address0, decod_er_1_address1, decod_er_1_address2, decod_er_1_address3,
       decod_er_3bit_1_out_2, decod_er_3bit_1_out_3, decod_er_3bit_1_out_4, decod_er_3bit_1_out_5, not_1_out,
       or_1_out, or_2_out, or_3_out, or_4_out;
  wire [2:0] L_data_out, R_data_out;
  wire [3:0] bit_extender_1_out_2;

  Clock clock_1 (.out(clock_1_out));
  not not_1 (not_1_out, controlunit_1_stop);
  Incrementer incrementer_1 (.pcinput(out_4), .pcincremented(out_3));
  PC pc_1 (.Clock(cu_steps_1_step4), .Enable(not_1_out), .pcinput(out_3), .pcoutput(out_4));
  or or_1 (or_1_out, cu_steps_1_step1, and_7_out);
  or or_2 (or_2_out, cu_steps_1_step1, and_8_out);
  and and_1 (and_1_out, and_9_out, and_5_out);
  or or_3 (or_3_out, cu_steps_1_step1, and_5_out);
  and and_2 (and_2_out, and_9_out, and_6_out);
  or or_4 (or_4_out, cu_steps_1_step1, and_6_out);
  and and_3 (and_3_out, and_9_out, and_7_out);
  and and_4 (and_4_out, and_9_out, and_8_out);
  Nibble nibble_1 (.Nibble_Out(out_1), .Enable(or_3_out), .Read_Write(and_1_out), .Data(bit_extender_1_out_2));
  Nibble nibble_2 (.Nibble_Out(out_2), .Enable(or_4_out), .Read_Write(and_2_out), .Data(bit_extender_1_out_2));
  Nibble nibble_3 (.Nibble_Out(out_8), .Enable(or_1_out), .Read_Write(and_9_out), .Data(bit_extender_1_out_2));
  Nibble nibble_4 (.Nibble_Out(out_9), .Enable(or_2_out), .Read_Write(and_4_out), .Data(bit_extender_1_out_2));
  decod_er decod_er_1 (
    .in_1(out_4), .address0(decod_er_1_address0), .address1(decod_er_1_address1),
    .address2(decod_er_1_address2), .address3(decod_er_1_address3));
  and and_5 (and_5_out, controlunit_1_out_4, decod_er_3bit_1_out_2);
  and and_6 (and_6_out, controlunit_1_out_4, decod_er_3bit_1_out_3);
  and and_7 (and_7_out, controlunit_1_out_4, decod_er_3bit_1_out_4);
  and and_8 (and_8_out, controlunit_1_out_4, decod_er_3bit_1_out_5);
  CU_steps cu_steps_1 (
    .in_1(out_14), .Clock(clock_1_out), .out_3(out_13), .Step1(cu_steps_1_step1), .Step2(cu_steps_1_step2),
    .Step3(cu_steps_1_step3), .Step4(cu_steps_1_step4));
  Step_Increment step_increment_1 (.Steps_in(out_13), .Steps_out(out_14));
  decod_er_3bit decod_er_3bit_1 (
    .out_5(decod_er_3bit_1_out_5), .in_1(out_7), .out_4(decod_er_3bit_1_out_4),
    .out_2(decod_er_3bit_1_out_2), .out_3(decod_er_3bit_1_out_3));
  InstructionRegister instructionregister_1 (
    .Nibble0(out_1), .address0(decod_er_1_address0), .Nibble1(out_2), .address1(decod_er_1_address1),
    .Nibble2(out_8), .address2(decod_er_1_address2), .Nibble3(out_9), .address3(decod_er_1_address3),
    .Clock(cu_steps_1_step2), .Bit0(out_7[0]), .Bit1(out_7[1]), .Bit2(out_7[2]), .Bit3(out_10));
  ControlUnit controlunit_1 (
    .Opcode(out_10), .Clock(cu_steps_1_step3), .Bits(out_7), .out_4(controlunit_1_out_4),
    .Stop(controlunit_1_stop));
  and and_9 (and_9_out, controlunit_1_out_4, cu_steps_1_step3);
  R_egister L (.Clock(cu_steps_1_step3), .Data_in(out_7), .Data_out(L_data_out));
  R_egister R (.Clock(cu_steps_1_step3), .Data_in(out_7), .Data_out(R_data_out));
  and and_10 (and_10_out, ~controlunit_1_out_4, ~controlunit_1_stop);  // AND_Gate
  and and_11 (and_11_out, cu_steps_1_step4, and_10_out);
  Bit_extender bit_extender_1 (.out_2(bit_extender_1_out_2), .in_1(out_5));
  ALU alu_1 (.L(L_data_out), .R(R_data_out), .DataOut(out_6), .Zero(alu_1_zero), .Overflow(alu_1_overflow));
  Status_Register status_register_1 (
    .Zero_in(alu_1_zero), .OF_in(alu_1_overflow), .Clock(and_11_out), .Zero_out(out_11), .OF_out(out_12));
  A_out_Register a_out_register_1 (.DataIn(out_6), .Clock(and_11_out), .DataOut(out_5));
endmodule

module Add_3Bits (
  input  [2:0] A,
  input  [2:0] B,
  output [2:0] R,
  output Zero,
  output Overflow
);

  wire add_1bit_1_cout, add_1bit_2_cout;

  // Probe on A
  // Probe on B
  Add_1Bit add_1bit_1 (.Sum(R[0]), .Cout(add_1bit_1_cout), .Cin(1'b0), .A(A[0]), .B(B[0]));
  Add_1Bit add_1bit_2 (.Sum(R[1]), .Cout(add_1bit_2_cout), .Cin(add_1bit_1_cout), .A(A[1]), .B(B[1]));
  Add_1Bit add_1bit_3 (.Sum(R[2]), .Cout(Overflow), .Cin(add_1bit_2_cout), .A(A[2]), .B(B[2]));
  // Probe on R
  nor nor_1 (Zero, R[0], R[1], R[2]);

  // Notes on the sheet:
  //   NATHALIE RAFFRAY 260682940
  //   MAKE SURE THAT YOU OPEN THIS PROJECT IN "LOGISIM-EVOLUTION"
  //   YOU CAN FIND "LOGISIM-EVOLUTION" PROGRAM IN THE ASSIGNMENT'S FOLDER
  //   DO NOT USE "LOGISIM" VERSION TO SOLVE THIS ASSIGNMENT!
endmodule

module Add_1Bit (
  input  Cin,
  input  A,
  input  B,
  output Cout,
  output Sum
);

  wire and_1_out, and_2_out, and_3_out, not_1_out, or_1_out;

  and and_1 (and_1_out, B, A);
  or or_1 (or_1_out, A, B);
  not not_1 (not_1_out, and_1_out);
  and and_2 (and_2_out, not_1_out, or_1_out);
  xor xor_1 (Sum, Cin, and_2_out);
  and and_3 (and_3_out, Cin, and_2_out);
  or or_2 (Cout, and_1_out, and_3_out);

  // Notes on the sheet:
  //   Nathalie Raffray 260682940
  //   MAKE SURE THAT YOU OPENED THIS PROJECT IN "LOGISIM-EVOLUTION"
  //   YOU CAN FIND "LOGISIM-EVOLUTION" PROGRAM IN THE ASSIGNMENT'S FOLDER
  //   DO NOT USE "LOGISIM" VERSION TO SOLVE THIS ASSIGNMENT!
endmodule

module Nibble (
  input  Read_Write,
  input  [3:0] Data,
  input  Enable,
  output [3:0] Nibble_Out
);

  wire and_1_out;

  // Probe on Data
  and and_1 (and_1_out, Read_Write, Enable);
  D_Flip_Flop d_ff_1 (.D(Data[0]), .clk(and_1_out), .Q(Nibble_Out[0]));  // open: Qn, preset, reset
  D_Flip_Flop d_ff_2 (.D(Data[1]), .clk(and_1_out), .Q(Nibble_Out[1]));  // open: Qn, preset, reset
  D_Flip_Flop d_ff_3 (.D(Data[2]), .clk(and_1_out), .Q(Nibble_Out[2]));  // open: Qn, preset, reset
  D_Flip_Flop d_ff_4 (.D(Data[3]), .clk(and_1_out), .Q(Nibble_Out[3]));  // open: Qn, preset, reset
  // Probe on Nibble_Out

  // Notes on the sheet:
  //   Read_Write = 1 performs write
endmodule

module multi_plexer (
  input  in_1,
  input  in_2,
  input  in_3,
  output out_4
);

  wire and_1_out, and_2_out, not_1_out;

  not not_1 (not_1_out, in_3);
  and and_1 (and_1_out, in_1, not_1_out);
  and and_2 (and_2_out, in_2, in_3);
  or or_1 (out_4, and_1_out, and_2_out);
endmodule

module PC (
  input  Clock,
  input  Enable,
  input  [1:0] pcinput,
  output [1:0] pcoutput
);

  wire and_1_out;

  and and_1 (and_1_out, Clock, Enable);
  D_Flip_Flop d_ff_1 (.D(pcinput[0]), .clk(and_1_out), .Q(pcoutput[0]));  // open: Qn, preset, reset
  D_Flip_Flop d_ff_2 (.D(pcinput[1]), .clk(and_1_out), .Q(pcoutput[1]));  // open: Qn, preset, reset
endmodule

module Incrementer (
  input  [1:0] pcinput,
  output [1:0] pcincremented
);

  wire add_1bit_1_cout;

  Add_1Bit add_1bit_1 (.Sum(pcincremented[0]), .Cout(add_1bit_1_cout), .A(1'b1), .B(pcinput[0]));  // open: Cin
  Add_1Bit add_1bit_2 (.Sum(pcincremented[1]), .Cin(add_1bit_1_cout), .A(1'b0), .B(pcinput[1]));  // open: Cout
endmodule

module decod_er (
  input  [1:0] in_1,
  output address0,
  output address1,
  output address2,
  output address3
);

  and and_1 (address0, ~in_1[0], ~in_1[1]);  // AND_Gate
  and and_2 (address1, in_1[0], ~in_1[1]);  // AND_Gate
  and and_3 (address2, ~in_1[0], in_1[1]);  // AND_Gate
  and and_4 (address3, in_1[0], in_1[1]);
endmodule

module InstructionRegister (
  input  [3:0] Nibble0,
  input  address0,
  input  [3:0] Nibble1,
  input  address1,
  input  [3:0] Nibble2,
  input  address2,
  input  [3:0] Nibble3,
  input  address3,
  input  Clock,
  output Bit0,
  output Bit1,
  output Bit2,
  output Bit3
);

  wire selector_4bits_1_out_9, selector_4bits_2_out_9, selector_4bits_3_out_9, selector_4bits_4_out_9;

  Selector_4bits selector_4bits_1 (
    .in_1(Nibble0[0]), .address0(address0), .in_3(Nibble1[0]), .address1(address1), .in_5(Nibble2[0]),
    .address2(address2), .in_7(Nibble3[0]), .address3(address3), .out_9(selector_4bits_1_out_9));
  Selector_4bits selector_4bits_2 (
    .in_1(Nibble0[1]), .address0(address0), .in_3(Nibble1[1]), .address1(address1), .in_5(Nibble2[1]),
    .address2(address2), .in_7(Nibble3[1]), .address3(address3), .out_9(selector_4bits_2_out_9));
  Selector_4bits selector_4bits_3 (
    .in_1(Nibble0[2]), .address0(address0), .in_3(Nibble1[2]), .address1(address1), .in_5(Nibble2[2]),
    .address2(address2), .in_7(Nibble3[2]), .address3(address3), .out_9(selector_4bits_3_out_9));
  Selector_4bits selector_4bits_4 (
    .in_1(Nibble0[3]), .address0(address0), .in_3(Nibble1[3]), .address1(address1), .in_5(Nibble2[3]),
    .address2(address2), .in_7(Nibble3[3]), .address3(address3), .out_9(selector_4bits_4_out_9));
  D_Flip_Flop d_ff_1 (.D(selector_4bits_1_out_9), .clk(Clock), .Q(Bit0));  // open: Qn, preset, reset
  D_Flip_Flop d_ff_2 (.D(selector_4bits_2_out_9), .clk(Clock), .Q(Bit1));  // open: Qn, preset, reset
  D_Flip_Flop d_ff_3 (.D(selector_4bits_3_out_9), .clk(Clock), .Q(Bit2));  // open: Qn, preset, reset
  D_Flip_Flop d_ff_4 (.D(selector_4bits_4_out_9), .clk(Clock), .Q(Bit3));  // open: Qn, preset, reset
endmodule

module Selector_4bits (
  input  in_1,
  input  address0,
  input  in_3,
  input  address1,
  input  in_5,
  input  address2,
  input  in_7,
  input  address3,
  output out_9
);

  wire and_1_out, and_2_out, and_3_out, and_4_out;

  and and_1 (and_1_out, in_1, address0);
  and and_2 (and_2_out, in_3, address1);
  and and_3 (and_3_out, in_5, address2);
  and and_4 (and_4_out, in_7, address3);
  or or_1 (out_9, and_1_out, and_2_out, and_3_out, and_4_out);
endmodule

module ControlUnit (
  input  Opcode,
  input  Clock,
  input  [2:0] Bits,
  output out_4,
  output Stop
);

  wire d_ff_1_q, nor_1_out;

  nor nor_1 (nor_1_out, Bits[0], Bits[1], Bits[2]);
  D_Flip_Flop d_ff_1 (.D(nor_1_out), .clk(Clock), .Q(d_ff_1_q));  // open: Qn, preset, reset
  and and_1 (Stop, d_ff_1_q, ~Opcode);  // AND_Gate

  assign out_4 = Opcode;
endmodule

module ALU_perhaps (
  input  [2:0] L,
  input  in_2,
  input  [2:0] R,
  input  [2:0] Address,
  input  Opcode,
  input  [2:0] in_6,
  input  [2:0] in_7,
  input  in_8,
  input  in_9,
  output [2:0] out_10,
  output Zero,
  output Overflow,
  output [2:0] out_13,
  output out_14,
  output out_15
);

  wire and_1_out, not_1_out, undriven, undriven_2;
  wire [2:0] add_3bits_1_r, Add_r;

  Add_3Bits Add (.A(L), .B(R), .R(Add_r), .Zero(Zero), .Overflow(Overflow));
  Add_3Bits add_3bits_1 (.A(in_6), .B(in_7), .R(add_3bits_1_r), .Zero(out_14), .Overflow(out_15));
  not not_1 (not_1_out, in_9);
  multi_plexer multi_plexer_1 (.in_2(Address[0]), .out_4(out_10[0]), .in_1(Add_r[0]), .in_3(Opcode));
  multi_plexer multi_plexer_2 (.in_2(Address[1]), .out_4(out_10[1]), .in_1(Add_r[1]), .in_3(Opcode));
  multi_plexer multi_plexer_3 (.in_2(Address[2]), .out_4(out_10[2]), .in_1(Add_r[2]), .in_3(Opcode));
  and and_1 (and_1_out, in_8, not_1_out);
  D_Flip_Flop d_ff_1 (.D(add_3bits_1_r[0]), .clk(and_1_out), .Q(out_13[0]));  // open: Qn, preset, reset
  D_Flip_Flop d_ff_2 (.D(add_3bits_1_r[1]), .clk(and_1_out), .Q(out_13[1]));  // open: Qn, preset, reset
  D_Flip_Flop d_ff_3 (.D(add_3bits_1_r[2]), .clk(and_1_out), .Q(out_13[2]));  // open: Qn, preset, reset
  D_Flip_Flop d_ff_4 (.D(undriven), .clk(in_2));  // open: Q, Qn, preset, reset
  D_Flip_Flop d_ff_5 (.D(undriven_2), .clk(in_2));  // open: Q, Qn, preset, reset

  // Notes on the sheet:
  //   cu increment
endmodule

module R_egister (
  input  Clock,
  input  [2:0] Data_in,
  output [2:0] Data_out
);

  D_Flip_Flop d_ff_1 (.D(Data_in[0]), .clk(Clock), .Q(Data_out[0]));  // open: Qn, preset, reset
  D_Flip_Flop d_ff_2 (.D(Data_in[1]), .clk(Clock), .Q(Data_out[1]));  // open: Qn, preset, reset
  D_Flip_Flop d_ff_3 (.D(Data_in[2]), .clk(Clock), .Q(Data_out[2]));  // open: Qn, preset, reset
endmodule

module ALU (
  input  [2:0] L,
  input  [2:0] R,
  output [2:0] DataOut,
  output Zero,
  output Overflow
);

  Add_3Bits add_3bits_1 (.A(L), .B(R), .R(DataOut), .Zero(Zero), .Overflow(Overflow));
endmodule

module A_out_Register (
  input  [2:0] DataIn,
  input  Clock,
  output [2:0] DataOut
);

  D_Flip_Flop d_ff_1 (.D(DataIn[0]), .clk(Clock), .Q(DataOut[0]));  // open: Qn, preset, reset
  D_Flip_Flop d_ff_2 (.D(DataIn[1]), .clk(Clock), .Q(DataOut[1]));  // open: Qn, preset, reset
  D_Flip_Flop d_ff_3 (.D(DataIn[2]), .clk(Clock), .Q(DataOut[2]));  // open: Qn, preset, reset
endmodule

module Status_Register (
  input  Zero_in,
  input  OF_in,
  input  Clock,
  output Zero_out,
  output OF_out
);

  D_Flip_Flop d_ff_1 (.D(Zero_in), .clk(Clock), .Q(Zero_out));  // open: Qn, preset, reset
  D_Flip_Flop d_ff_2 (.D(OF_in), .clk(Clock), .Q(OF_out));  // open: Qn, preset, reset
endmodule

module Bit_extender (
  input  [2:0] in_1,
  output [3:0] out_2
);


  assign out_2 = {1'b0, in_1};
endmodule

module decod_er_3bit (
  input  [2:0] in_1,
  output out_2,
  output out_3,
  output out_4,
  output out_5
);

  and and_1 (out_2, ~in_1[0], ~in_1[1], ~in_1[2]);  // AND_Gate
  and and_2 (out_3, in_1[0], ~in_1[1], ~in_1[2]);  // AND_Gate
  and and_3 (out_4, ~in_1[0], in_1[1], ~in_1[2]);  // AND_Gate
  and and_4 (out_5, in_1[0], in_1[1], ~in_1[2]);  // AND_Gate
endmodule

module CU_steps (
  input  [1:0] in_1,
  input  Clock,
  output [1:0] out_3,
  output Step1,
  output Step2,
  output Step3,
  output Step4
);

  D_Flip_Flop d_ff_1 (.D(in_1[0]), .clk(Clock), .Q(out_3[0]));  // open: Qn, preset, reset
  D_Flip_Flop d_ff_2 (.D(in_1[1]), .clk(Clock), .Q(out_3[1]));  // open: Qn, preset, reset
  and and_1 (Step1, ~out_3[0], ~out_3[1]);  // AND_Gate
  and and_2 (Step2, out_3[0], ~out_3[1]);  // AND_Gate
  and and_3 (Step3, ~out_3[0], out_3[1]);  // AND_Gate
  and and_4 (Step4, out_3[0], out_3[1]);
endmodule

module Step_Increment (
  input  [1:0] Steps_in,
  output [1:0] Steps_out
);

  wire add_1bit_1_cout;

  Add_1Bit add_1bit_1 (.Sum(Steps_out[0]), .Cout(add_1bit_1_cout), .A(Steps_in[0]), .B(1'b1));  // open: Cin
  Add_1Bit add_1bit_2 (.Sum(Steps_out[1]), .Cin(add_1bit_1_cout), .A(Steps_in[1]), .B(1'b0));  // open: Cout
endmodule
